// Logisim project Signal cycle.circ as structural Verilog: 14 circuits, main circuit Type Decode
module Type_Decode (
  input  [6:0] in_1,
  output For_I_type_addi,
  output out_3,
  output out_4,
  output out_5,
  output out_6,
  output out_7,
  output For_I_type_LUI,
  output out_9,
  output out_10
);

  Comparator #(.width(7)) comparator_1 (.a(in_1), .b(7'b0010011), .eq(For_I_type_addi));  // open: gt, lt
  Comparator #(.width(7)) comparator_2 (.a(in_1), .b(7'b0110011), .eq(out_5));  // open: gt, lt
  Comparator #(.width(7)) comparator_3 (.a(in_1), .b(7'b0100011), .eq(out_6));  // open: gt, lt
  Comparator #(.width(7)) comparator_4 (.a(in_1), .b(7'b0010111), .eq(out_7));  // open: gt, lt
  Comparator #(.width(7)) comparator_5 (.a(in_1), .b(7'b1101111), .eq(out_9));  // open: gt, lt
  Comparator #(.width(7)) comparator_6 (.a(in_1), .b(7'b1100011), .eq(out_10));  // open: gt, lt
  Comparator #(.width(7)) comparator_7 (.a(in_1), .b(7'b1100111), .eq(out_3));  // open: gt, lt
  Comparator #(.width(7)) comparator_8 (.a(in_1), .b(7'b0110111), .eq(For_I_type_LUI));  // open: gt, lt
  Comparator #(.width(7)) comparator_9 (.a(in_1), .b(7'b0000011), .eq(out_4));  // open: gt, lt

  // Notes on the sheet:
  //   For R-type
  //   For S-type
  //   For U-type(AUIPC)
  //   For UJ-type
  //   For SB-type
  //   For I-type(jalr)
  //   For I-type(lw)
endmodule

module Immediate_generation (
  input  [31:0] Instruction,
  input  [31:0] PC,
  output [31:0] out_3,
  output [31:0] out_4,
  output [31:0] out_5,
  output [31:0] out_6,
  output [31:0] out_7
);

  wire [19:0] shifter_1_out;
  wire [31:0] bit_extender_4_out, bit_extender_5_out;

  Shifter #(.width(20)) shifter_1 (.in(Instruction[31:12]), .\dist (5'b01100), .out(shifter_1_out));
  assign out_3 = {{20{Instruction[31]}}, Instruction[31:20]};  // Bit_Extender bit_extender_1
  assign out_7 = {{12{shifter_1_out[19]}}, shifter_1_out};  // Bit_Extender bit_extender_2
  assign out_4 = {{20{Instruction[31]}}, {Instruction[31:25], Instruction[11:7]}};  // Bit_Extender bit_extender_3
  assign bit_extender_4_out = {{19{Instruction[31]}}, {Instruction[31], Instruction[7], Instruction[30:25], Instruction[11:8], 1'b0}};  // Bit_Extender bit_extender_4
  assign bit_extender_5_out = {{11{Instruction[31]}}, {Instruction[31], Instruction[19:12], Instruction[20], Instruction[30:21], 1'b0}};  // Bit_Extender bit_extender_5
  Adder #(.width(32)) adder_1 (.a(bit_extender_4_out), .b(PC), .out(out_5));  // open: cin, cout
  Adder #(.width(32)) adder_2 (.a(bit_extender_5_out), .b(PC), .out(out_6));  // open: cin, cout

  // Notes on the sheet:
  //   I-Type
  //   S-Type
  //   SB-Type
  //   UJ-Type
  //   U-Type
endmodule

module Control_Decode (
  input  Addi,
  input  jalr,
  input  lw,
  input  R_type,
  input  S_type,
  input  AUIPC,
  input  LUI,
  input  UJ_type,
  input  SB_type,
  input  in_10,
  input  [2:0] in_11,
  output Reg_write,
  output Branch,
  output Store,
  output Load,
  output Mem2Reg,
  output [1:0] out_17,
  output op_B_sel,
  output [1:0] extend_sel,
  output [1:0] Next_PC_sel,
  output [3:0] out_21
);

  wire alu_op_1_output0, alu_op_1_output1, alu_op_1_output2, or_1_out, or_2_out, or_3_out;

  or or_1 (or_1_out, Addi, jalr, lw);
  or or_2 (or_2_out, AUIPC, LUI);
  or or_3 (or_3_out, UJ_type, jalr);
  Imm_sel imm_sel_1 (.Itype(or_1_out), .Utype(S_type), .Stype(or_2_out), .A(extend_sel[1]), .B(extend_sel[0]));
  ALU_op alu_op_1 (
    .RType(R_type), .Load(Addi), .Addi(jalr), .Jalr(lw), .Store(S_type), .AUIPC(AUIPC), .LUI(LUI),
    .Jal(UJ_type), .Output2(alu_op_1_output2), .Output1(alu_op_1_output1), .Output0(alu_op_1_output0));
  or or_4 (Reg_write, Addi, jalr, lw, R_type, AUIPC, LUI, UJ_type);
  NEXT_PC_SELECT next_pc_select_1 (
    .A(Next_PC_sel[0]), .Branch(SB_type), .B(Next_PC_sel[1]), .jal(UJ_type), .jalr(jalr));  // open: PCplus4
  Operand_A_Sel operand_a_sel_1 (
    .PC(LUI), .PCplus4(or_3_out), .zero(1'b0), .Output1(out_17[1]), .Output0(out_17[0]));  // open: rs1
  or or_5 (op_B_sel, R_type, S_type, SB_type);
  ALU_Control alu_control_1 (
    .Func7_30(in_10), .ALU_op_0(alu_op_1_output0), .ALU_op_1(alu_op_1_output1), .ALU_op_2(alu_op_1_output2),
    .Func3_0(in_11[0]), .Func3_1(in_11[1]), .Func3_2(in_11[2]), .Output3(out_21[3]), .Output2(out_21[2]),
    .Output1(out_21[1]), .Output0(out_21[0]));

  assign Branch = SB_type;
  assign Load = lw;
  assign Mem2Reg = lw;
  assign Store = S_type;
endmodule

module Control_Unit (
  input  [6:0] in_1,
  input  [2:0] in_2,
  input  in_3,
  output Reg_write,
  output Branch,
  output Store,
  output Load,
  output Mem2reg,
  output [1:0] Op_A_sel,
  output Op_B_sel,
  output [1:0] Imm_sel,
  output [1:0] Next_PC_sel,
  output [3:0] ALU_control
);

  wire type_decode_1_for_i_type_addi, type_decode_1_for_i_type_lui, type_decode_1_out_3, type_decode_1_out_4,
       type_decode_1_out_5, type_decode_1_out_6, type_decode_1_out_7, type_decode_1_out_9,
       type_decode_1_out_10;

  Type_Decode type_decode_1 (
    .in_1(in_1), .For_I_type_addi(type_decode_1_for_i_type_addi), .out_3(type_decode_1_out_3),
    .out_4(type_decode_1_out_4), .out_5(type_decode_1_out_5), .out_6(type_decode_1_out_6),
    .out_7(type_decode_1_out_7), .For_I_type_LUI(type_decode_1_for_i_type_lui), .out_9(type_decode_1_out_9),
    .out_10(type_decode_1_out_10));
  Control_Decode control_decode_1 (
    .Reg_write(Reg_write), .Branch(Branch), .Store(Store), .Load(Load), .Mem2Reg(Mem2reg), .out_17(Op_A_sel),
    .op_B_sel(Op_B_sel), .extend_sel(Imm_sel), .Next_PC_sel(Next_PC_sel),
    .Addi(type_decode_1_for_i_type_addi), .jalr(type_decode_1_out_3), .lw(type_decode_1_out_4),
    .R_type(type_decode_1_out_5), .S_type(type_decode_1_out_6), .AUIPC(type_decode_1_out_7),
    .LUI(type_decode_1_for_i_type_lui), .UJ_type(type_decode_1_out_9), .SB_type(type_decode_1_out_10),
    .in_11(in_2), .in_10(in_3), .out_21(ALU_control));
endmodule

module Imm_sel (
  input  Itype,
  input  Utype,
  input  Stype,
  output A,
  output B
);

  or or_1 (A, Stype, Utype);
  or or_2 (B, Utype, Itype);
endmodule

module NEXT_PC_SELECT (
  input  PCplus4,
  input  Branch,
  input  jal,
  input  jalr,
  output A,
  output B
);

  or or_1 (A, jalr, jal);
  or or_2 (B, jalr, Branch);
endmodule

module Reg_File (
  input  [31:0] in_1,
  input  in_2,
  input  [4:0] in_3,
  input  [4:0] in_4,
  input  [4:0] in_5,
  input  in_6,
  output [31:0] out_7,
  output [31:0] out_8
);

  wire decoder_1_out1, decoder_1_out2, decoder_1_out3, decoder_1_out4, decoder_1_out5, decoder_1_out6,
       decoder_1_out7, decoder_1_out8, decoder_1_out9, decoder_1_out10, decoder_1_out11, decoder_1_out12,
       decoder_1_out13, decoder_1_out14, decoder_1_out15, decoder_1_out16, decoder_1_out17, decoder_1_out18,
       decoder_1_out19, decoder_1_out20, decoder_1_out21, decoder_1_out22, decoder_1_out23, decoder_1_out24,
       decoder_1_out25, decoder_1_out26, decoder_1_out27, decoder_1_out28, decoder_1_out29, decoder_1_out30,
       decoder_1_out31;
  wire [31:0] register_1_q, register_2_q, register_3_q, register_4_q, register_5_q, register_6_q,
       register_7_q, register_8_q, register_9_q, register_10_q, register_11_q, register_12_q, register_13_q,
       register_14_q, register_15_q, register_16_q, register_17_q, register_18_q, register_19_q,
       register_20_q, register_21_q, register_22_q, register_23_q, register_24_q, register_25_q,
       register_26_q, register_27_q, register_28_q, register_29_q, register_30_q, register_31_q;

  Decoder #(.select(5), .disabled(0)) decoder_1 (
    .out1(decoder_1_out1), .out2(decoder_1_out2), .out3(decoder_1_out3), .out4(decoder_1_out4),
    .out5(decoder_1_out5), .out6(decoder_1_out6), .out7(decoder_1_out7), .out8(decoder_1_out8),
    .out9(decoder_1_out9), .out10(decoder_1_out10), .out11(decoder_1_out11), .out12(decoder_1_out12),
    .out13(decoder_1_out13), .out14(decoder_1_out14), .out15(decoder_1_out15), .out16(decoder_1_out16),
    .out17(decoder_1_out17), .out18(decoder_1_out18), .out19(decoder_1_out19), .out20(decoder_1_out20),
    .out21(decoder_1_out21), .out22(decoder_1_out22), .out23(decoder_1_out23), .out24(decoder_1_out24),
    .out25(decoder_1_out25), .out26(decoder_1_out26), .out27(decoder_1_out27), .out28(decoder_1_out28),
    .out29(decoder_1_out29), .out30(decoder_1_out30), .out31(decoder_1_out31), .sel(in_4), .en(in_2));  // open: out0
  Register #(.width(32)) register_1 (.D(in_1), .en(decoder_1_out1), .Q(register_1_q), .clk(in_6));  // open: clr
  Register #(.width(32)) register_2 (.D(in_1), .en(decoder_1_out2), .Q(register_2_q), .clk(in_6));  // open: clr
  Register #(.width(32)) register_3 (.D(in_1), .en(decoder_1_out3), .Q(register_3_q), .clk(in_6));  // open: clr
  Register #(.width(32)) register_4 (.D(in_1), .en(decoder_1_out4), .Q(register_4_q), .clk(in_6));  // open: clr
  Register #(.width(32)) register_5 (.D(in_1), .en(decoder_1_out5), .Q(register_5_q), .clk(in_6));  // open: clr
  Register #(.width(32)) register_6 (.D(in_1), .en(decoder_1_out6), .Q(register_6_q), .clk(in_6));  // open: clr
  Register #(.width(32)) register_7 (.D(in_1), .en(decoder_1_out7), .Q(register_7_q), .clk(in_6));  // open: clr
  Register #(.width(32)) register_8 (.D(in_1), .en(decoder_1_out8), .Q(register_8_q), .clk(in_6));  // open: clr
  Register #(.width(32)) register_9 (.D(in_1), .en(decoder_1_out9), .Q(register_9_q), .clk(in_6));  // open: clr
  Register #(.width(32)) register_10 (.D(in_1), .en(decoder_1_out10), .Q(register_10_q), .clk(in_6));  // open: clr
  Register #(.width(32)) register_11 (.D(in_1), .en(decoder_1_out11), .Q(register_11_q), .clk(in_6));  // open: clr
  Register #(.width(32)) register_12 (.D(in_1), .en(decoder_1_out12), .Q(register_12_q), .clk(in_6));  // open: clr
  Register #(.width(32)) register_13 (.D(in_1), .en(decoder_1_out13), .Q(register_13_q), .clk(in_6));  // open: clr
  Register #(.width(32)) register_14 (.D(in_1), .en(decoder_1_out14), .Q(register_14_q), .clk(in_6));  // open: clr
  Register #(.width(32)) register_15 (.D(in_1), .en(decoder_1_out15), .Q(register_15_q), .clk(in_6));  // open: clr
  Register #(.width(32)) register_16 (.D(in_1), .en(decoder_1_out16), .Q(register_16_q), .clr(in_6));  // open: clk
  Register #(.width(32)) register_17 (.D(in_1), .en(decoder_1_out17), .Q(register_17_q), .clk(in_6));  // open: clr
  Register #(.width(32)) register_18 (.D(in_1), .en(decoder_1_out18), .Q(register_18_q), .clk(in_6));  // open: clr
  Register #(.width(32)) register_19 (.D(in_1), .en(decoder_1_out19), .Q(register_19_q), .clk(in_6));  // open: clr
  Register #(.width(32)) register_20 (.D(in_1), .en(decoder_1_out20), .Q(register_20_q), .clk(in_6));  // open: clr
  Register #(.width(32)) register_21 (.D(in_1), .en(decoder_1_out21), .Q(register_21_q), .clk(in_6));  // open: clr
  Register #(.width(32)) register_22 (.D(in_1), .en(decoder_1_out22), .Q(register_22_q), .clk(in_6));  // open: clr
  Register #(.width(32)) register_23 (.D(in_1), .en(decoder_1_out23), .Q(register_23_q), .clk(in_6));  // open: clr
  Register #(.width(32)) register_24 (.D(in_1), .en(decoder_1_out24), .Q(register_24_q), .clk(in_6));  // open: clr
  Register #(.width(32)) register_25 (.D(in_1), .en(decoder_1_out25), .Q(register_25_q), .clk(in_6));  // open: clr
  Register #(.width(32)) register_26 (.D(in_1), .en(decoder_1_out26), .Q(register_26_q), .clk(in_6));  // open: clr
  Register #(.width(32)) register_27 (.D(in_1), .en(decoder_1_out27), .Q(register_27_q), .clk(in_6));  // open: clr
  Register #(.width(32)) register_28 (.D(in_1), .en(decoder_1_out28), .Q(register_28_q), .clk(in_6));  // open: clr
  Register #(.width(32)) register_29 (.D(in_1), .en(decoder_1_out29), .Q(register_29_q), .clk(in_6));  // open: clr
  Register #(.width(32)) register_30 (.D(in_1), .en(decoder_1_out30), .Q(register_30_q), .clk(in_6));  // open: clr
  Register #(.width(32)) register_31 (.D(in_1), .en(decoder_1_out31), .Q(register_31_q), .clk(in_6));  // open: clr
  Multiplexer #(.select(5), .width(32)) multiplexer_1 (
    .in0({32{1'b0}}), .in1(register_1_q), .in2(register_2_q), .in3(register_3_q), .in4(register_4_q),
    .in5(register_5_q), .in6(register_6_q), .in7(register_7_q), .in8(register_8_q), .in9(register_9_q),
    .in10(register_10_q), .in11(register_11_q), .in12(register_12_q), .in13(register_13_q),
    .in14(register_14_q), .in15(register_15_q), .in16(register_16_q), .in17(register_17_q),
    .in18(register_18_q), .in19(register_19_q), .in20(register_20_q), .in21(register_21_q),
    .in22(register_22_q), .in23(register_23_q), .in24(register_24_q), .in25(register_25_q),
    .in26(register_26_q), .in27(register_27_q), .in28(register_28_q), .in29(register_29_q),
    .in30(register_30_q), .in31(register_31_q), .out(out_7), .sel(in_3));  // open: en
  Multiplexer #(.select(5), .width(32)) multiplexer_2 (
    .in0({32{1'b0}}), .in1(register_1_q), .in2(register_2_q), .in3(register_3_q), .in4(register_4_q),
    .in5(register_5_q), .in6(register_6_q), .in7(register_7_q), .in8(register_8_q), .in9(register_9_q),
    .in10(register_10_q), .in11(register_11_q), .in12(register_12_q), .in13(register_13_q),
    .in14(register_14_q), .in15(register_15_q), .in16(register_16_q), .in17(register_17_q),
    .in18(register_18_q), .in19(register_19_q), .in20(register_20_q), .in21(register_21_q),
    .in22(register_22_q), .in23(register_23_q), .in24(register_24_q), .in25(register_25_q),
    .in26(register_26_q), .in27(register_27_q), .in28(register_28_q), .in29(register_29_q),
    .in30(register_30_q), .in31(register_31_q), .out(out_8), .sel(in_5));  // open: en
endmodule

module ALU (
  input  [3:0] in_1,
  input  [31:0] in_2,
  input  [31:0] in_3,
  output [31:0] out_4
);

  wire comparator_1_gt, comparator_2_gt;
  wire [31:0] adder_1_out, and_1_out, bit_extender_1_out, bit_extender_2_out, or_1_out, shifter_1_out,
       shifter_2_out, shifter_3_out, subtractor_1_out, xor_1_out;

  Adder #(.width(32)) adder_1 (.a(in_2), .b(in_3), .out(adder_1_out));  // open: cin, cout
  Subtractor #(.width(32)) subtractor_1 (.a(in_2), .b(in_3), .out(subtractor_1_out));  // open: bin, bout
  assign and_1_out = in_2 & in_3;  // AND_Gate and_1, 32 bits wide
  assign or_1_out = in_2 | in_3;  // OR_Gate or_1, 32 bits wide
  assign xor_1_out = in_2 ^ in_3;  // XOR_Gate xor_1, 32 bits wide
  Shifter #(.width(32)) shifter_1 (.in(in_2), .\dist (in_3[4:0]), .out(shifter_1_out));
  Shifter #(.width(32), .shift("lr")) shifter_2 (.in(in_2), .\dist (in_3[4:0]), .out(shifter_2_out));
  Shifter #(.width(32), .shift("ar")) shifter_3 (.in(in_2), .\dist (in_3[4:0]), .out(shifter_3_out));
  Comparator #(.width(32)) comparator_1 (.a(in_2), .b(in_3), .gt(comparator_1_gt));  // open: eq, lt
  Comparator #(.width(32), .mode("unsigned")) comparator_2 (.a(in_2), .b(in_3), .gt(comparator_2_gt));  // open: eq, lt
  assign bit_extender_1_out = {{31{1'b0}}, comparator_1_gt};  // Bit_Extender bit_extender_1
  assign bit_extender_2_out = {{31{1'b0}}, comparator_2_gt};  // Bit_Extender bit_extender_2
  Multiplexer #(.select(4), .width(32)) multiplexer_1 (
    .in0(adder_1_out), .in1(subtractor_1_out), .in2(and_1_out), .in3(or_1_out), .in4(xor_1_out),
    .in5(shifter_1_out), .in6(shifter_2_out), .in7(bit_extender_1_out), .in8(bit_extender_2_out),
    .in9(shifter_3_out), .in15(in_2), .out(out_4), .sel(in_1));  // open: in10, in11, in12, in13, in14, en

  // Notes on the sheet:
  //   A
  //   B
  //   Add, Addi
  //   Sub
  //   And
  //   Or
  //   Xor
  //   Sll
  //   Srl
  //   Sra
  //   Slt
  //   Sltu
  //   Jal, Jalr
endmodule

module ALU_op (
  input  RType,
  input  Load,
  input  Addi,
  input  Jalr,
  input  Store,
  input  AUIPC,
  input  LUI,
  input  Jal,
  output Output2,
  output Output1,
  output Output0
);

  or or_1 (Output2, Jal, LUI, AUIPC, Store);
  or or_2 (Output1, Jal, LUI, Jalr, Addi);
  or or_3 (Output0, Jal, AUIPC, Jalr, Load);
endmodule

module ALU_Control (
  input  Func7_30,
  input  ALU_op_0,
  input  ALU_op_1,
  input  ALU_op_2,
  input  Func3_0,
  input  Func3_1,
  input  Func3_2,
  output Output3,
  output Output2,
  output Output1,
  output Output0
);

  wire and_1_out, and_2_out, and_3_out, and_4_out, and_5_out, and_6_out, and_7_out, and_8_out, and_9_out,
       and_10_out, and_11_out, and_12_out, and_13_out, and_14_out, and_15_out, and_16_out, and_17_out,
       not_1_out, not_2_out, not_3_out, not_4_out, not_5_out, not_6_out, not_7_out, not_8_out, not_9_out,
       not_10_out, not_11_out, not_12_out, not_13_out, not_14_out, not_15_out, not_16_out, not_17_out,
       not_18_out, not_19_out, not_20_out, not_21_out, not_22_out, not_23_out, not_24_out, not_25_out,
       not_26_out, not_27_out, not_28_out, not_29_out, not_30_out, not_31_out, not_32_out, not_33_out,
       not_34_out, not_35_out;

  not not_1 (not_1_out, ALU_op_0);
  not not_2 (not_2_out, Func3_0);
  not not_3 (not_3_out, ALU_op_1);
  not not_4 (not_4_out, ALU_op_2);
  not not_5 (not_5_out, Func3_1);
  not not_6 (not_6_out, Func3_2);
  not not_7 (not_7_out, ALU_op_0);
  not not_8 (not_8_out, Func3_1);
  not not_9 (not_9_out, Func7_30);
  not not_10 (not_10_out, ALU_op_0);
  not not_11 (not_11_out, Func3_1);
  not not_12 (not_12_out, ALU_op_0);
  not not_13 (not_13_out, ALU_op_2);
  not not_14 (not_14_out, Func3_0);
  not not_15 (not_15_out, Func3_2);
  not not_16 (not_16_out, ALU_op_0);
  not not_17 (not_17_out, Func3_1);
  not not_18 (not_18_out, Func3_2);
  not not_19 (not_19_out, ALU_op_0);
  not not_20 (not_20_out, ALU_op_2);
  not not_21 (not_21_out, Func3_2);
  not not_22 (not_22_out, Func7_30);
  not not_23 (not_23_out, ALU_op_0);
  not not_24 (not_24_out, ALU_op_0);
  not not_25 (not_25_out, ALU_op_0);
  not not_26 (not_26_out, Func3_0);
  not not_27 (not_27_out, Func3_1);
  not not_28 (not_28_out, ALU_op_0);
  not not_29 (not_29_out, ALU_op_2);
  not not_30 (not_30_out, Func3_2);
  not not_31 (not_31_out, ALU_op_1);
  not not_32 (not_32_out, ALU_op_2);
  not not_33 (not_33_out, Func3_1);
  not not_34 (not_34_out, ALU_op_0);
  not not_35 (not_35_out, Func3_1);
  and and_1 (and_1_out, not_1_out, not_2_out, Func3_1, Func3_2);
  and and_2 (and_2_out, not_3_out, not_4_out, Func3_0, not_5_out, not_6_out);
  and and_3 (and_3_out, ALU_op_1, ALU_op_2);
  and and_4 (and_4_out, Func7_30, not_7_out, not_8_out, Func3_2);
  and and_5 (and_5_out, not_9_out, not_10_out, not_11_out, Func3_2);
  and and_6 (and_6_out, not_12_out, not_13_out, not_14_out, Func3_1, not_15_out);
  and and_7 (and_7_out, not_16_out, ALU_op_1, Func3_0, not_17_out, not_18_out);
  and and_8 (and_8_out, ALU_op_1, ALU_op_2);
  and and_9 (and_9_out, not_19_out, not_20_out, Func3_1, not_21_out);
  and and_10 (and_10_out, not_22_out, not_23_out, Func3_0, Func3_2);
  and and_11 (and_11_out, not_24_out, Func3_0, Func3_1);
  and and_12 (and_12_out, ALU_op_1, ALU_op_2);
  and and_13 (and_13_out, not_25_out, not_26_out, not_27_out, Func3_2);
  and and_14 (and_14_out, not_28_out, not_29_out, Func3_1, not_30_out);
  and and_15 (and_15_out, ALU_op_1, ALU_op_2);
  and and_16 (and_16_out, Func7_30, not_31_out, not_32_out, not_33_out);
  and and_17 (and_17_out, Func7_30, not_34_out, not_35_out, Func3_2);
  or or_1 (Output3, and_1_out, and_2_out, and_3_out, and_4_out);
  or or_2 (Output2, and_5_out, and_6_out, and_7_out, and_8_out);
  or or_3 (Output1, and_9_out, and_10_out, and_11_out, and_12_out);
  or or_4 (Output0, and_13_out, and_14_out, and_15_out, and_16_out, and_17_out);
endmodule

module Operand_A_Sel (
  input  rs1,
  input  PC,
  input  PCplus4,
  input  zero,
  output Output1,
  output Output0
);

  or or_1 (Output1, zero, PCplus4);
  or or_2 (Output0, zero, PC);
endmodule

module Branch_Module (
  input  [31:0] in_1,
  input  [31:0] in_2,
  input  in_3,
  input  [2:0] Func_3,
  output out_5
);

  wire comparator_1_eq, comparator_2_lt, comparator_3_eq, comparator_4_eq, comparator_4_gt, comparator_5_lt,
       comparator_6_eq, comparator_6_gt, not_1_out, or_1_out, or_2_out;

  Comparator #(.width(32)) comparator_1 (.a(in_1), .b(in_2), .eq(comparator_1_eq));  // open: gt, lt
  Comparator #(.width(32)) comparator_2 (.a(in_1), .b(in_2), .lt(comparator_2_lt));  // open: gt, eq
  Comparator #(.width(32)) comparator_3 (.a(in_1), .b(in_2), .eq(comparator_3_eq));  // open: gt, lt
  Comparator #(.width(32)) comparator_4 (.a(in_1), .b(in_2), .gt(comparator_4_gt), .eq(comparator_4_eq));  // open: lt
  Comparator #(.width(32), .mode("unsigned")) comparator_5 (.a(in_1), .b(in_2), .lt(comparator_5_lt));  // open: gt, eq
  Comparator #(.width(32), .mode("unsigned")) comparator_6 (
    .a(in_1), .b(in_2), .gt(comparator_6_gt), .eq(comparator_6_eq));  // open: lt
  not not_1 (not_1_out, comparator_3_eq);
  or or_1 (or_1_out, comparator_4_gt, comparator_4_eq);
  or or_2 (or_2_out, comparator_6_gt, comparator_6_eq);
  Multiplexer #(.select(3)) multiplexer_1 (
    .in0(comparator_1_eq), .in1(not_1_out), .in4(comparator_2_lt), .in5(or_1_out), .in6(comparator_5_lt),
    .in7(or_2_out), .out(out_5), .sel(Func_3));  // open: in2, in3, en

  // Notes on the sheet:
  //   A
  //   B
  //   Beq
  //   Blt
  //   Bge
  //   Bgeu
  //   Bne
  //   Bltu
endmodule

module jalr (
  input  [31:0] in_1,
  input  [31:0] in_2,
  output [31:0] out_3
);

  Adder #(.width(32)) adder_1 (.a(in_1), .b(in_2), .out(out_3));  // open: cin, cout

  // Notes on the sheet:
  //   RS1
  //    I type Imm
endmodule

module Top (
  output [31:0] out_1
);

  wire branch_module_1_out_5, button_1_out, clock_1_out, control_unit_1_branch, control_unit_1_load,
       control_unit_1_mem2reg, control_unit_1_op_b_sel, control_unit_1_reg_write, control_unit_1_store;
  wire [1:0] control_unit_1_imm_sel, control_unit_1_next_pc_sel, control_unit_1_op_a_sel;
  wire [3:0] control_unit_1_alu_control;
  wire [11:0] alu_1_out_4_2, register_1_q_2;
  wire [31:0] adder_1_out, alu_1_out_4, immediate_generation_1_out_3, immediate_generation_1_out_4,
       immediate_generation_1_out_5, immediate_generation_1_out_6, immediate_generation_1_out_7,
       jalr_1_out_3, multiplexer_1_out, multiplexer_2_out, multiplexer_3_out, multiplexer_4_out,
       multiplexer_5_out, ram_1_data, reg_file_1_out_7, reg_file_1_out_8, register_1_q, rom_1_data;

  Clock clock_1 (.out(clock_1_out));
  Button button_1 (.out(button_1_out));
  Multiplexer #(.select(2), .width(32), .enable("false")) multiplexer_1 (
    .in0(adder_1_out), .in1(multiplexer_2_out), .in2(immediate_generation_1_out_6), .in3(jalr_1_out_3),
    .out(multiplexer_1_out), .sel(control_unit_1_next_pc_sel));
  Register #(.width(32)) register_1 (
    .D(multiplexer_1_out), .Q({register_1_q[31:14], register_1_q_2, register_1_q[1:0]}), .clk(clock_1_out),
    .clr(button_1_out));  // open: en
  Multiplexer #(.width(32), .enable("false")) multiplexer_2 (
    .in0(adder_1_out), .in1(immediate_generation_1_out_5), .out(multiplexer_2_out),
    .sel(branch_module_1_out_5));
  Adder #(.width(32)) adder_1 (
    .a({register_1_q[31:14], register_1_q_2, register_1_q[1:0]}), .b(32'h4), .out(adder_1_out));  // open: cin, cout
  jalr jalr_1 (.in_1(reg_file_1_out_7), .in_2(immediate_generation_1_out_3), .out_3(jalr_1_out_3));
  Branch_Module branch_module_1 (
    .Func_3(rom_1_data[14:12]), .out_5(branch_module_1_out_5), .in_1(reg_file_1_out_7),
    .in_2(reg_file_1_out_8), .in_3(control_unit_1_branch));
  ROM #(.addrWidth(12), .dataWidth(32)) rom_1 (.addr(register_1_q_2), .data(rom_1_data));  // open: sel
  Control_Unit control_unit_1 (
    .in_1(rom_1_data[6:0]), .Reg_write(control_unit_1_reg_write), .Branch(control_unit_1_branch),
    .Store(control_unit_1_store), .Load(control_unit_1_load), .Mem2reg(control_unit_1_mem2reg),
    .Op_A_sel(control_unit_1_op_a_sel), .Op_B_sel(control_unit_1_op_b_sel), .Imm_sel(control_unit_1_imm_sel),
    .Next_PC_sel(control_unit_1_next_pc_sel), .in_2(rom_1_data[14:12]), .in_3(rom_1_data[30]),
    .ALU_control(control_unit_1_alu_control));
  Reg_File reg_file_1 (
    .in_2(control_unit_1_reg_write), .in_3(rom_1_data[19:15]), .in_4(rom_1_data[11:7]),
    .in_5(rom_1_data[24:20]), .out_7(reg_file_1_out_7), .out_8(reg_file_1_out_8), .in_1(out_1),
    .in_6(clock_1_out));
  Immediate_generation immediate_generation_1 (
    .Instruction(rom_1_data), .PC({register_1_q[31:14], register_1_q_2, register_1_q[1:0]}),
    .out_3(immediate_generation_1_out_3), .out_4(immediate_generation_1_out_4),
    .out_5(immediate_generation_1_out_5), .out_6(immediate_generation_1_out_6),
    .out_7(immediate_generation_1_out_7));
  Multiplexer #(.select(2), .width(32), .enable("false")) multiplexer_3 (
    .in1(immediate_generation_1_out_3), .in2(immediate_generation_1_out_4),
    .in3(immediate_generation_1_out_7), .out(multiplexer_3_out), .sel(control_unit_1_imm_sel));  // open: in0
  Multiplexer #(.select(2), .width(32), .enable("false")) multiplexer_4 (
    .in0(reg_file_1_out_7), .in1({register_1_q[31:14], register_1_q_2, register_1_q[1:0]}),
    .in2(adder_1_out), .in3({32{1'b0}}), .out(multiplexer_4_out), .sel(control_unit_1_op_a_sel));
  Multiplexer #(.width(32), .enable("false")) multiplexer_5 (
    .in0(multiplexer_3_out), .in1(reg_file_1_out_8), .out(multiplexer_5_out), .sel(control_unit_1_op_b_sel));
  ALU alu_1 (
    .in_1(control_unit_1_alu_control), .in_2(multiplexer_4_out), .in_3(multiplexer_5_out),
    .out_4({alu_1_out_4[31:14], alu_1_out_4_2, alu_1_out_4[1:0]}));
  RAM #(.addrWidth(12), .dataWidth(32), .bus("separate")) ram_1 (
    .addr(alu_1_out_4_2), .din(reg_file_1_out_8), .data(ram_1_data), .str(control_unit_1_store),
    .clk(clock_1_out), .ld(control_unit_1_load), .clr(button_1_out));  // open: sel
  Multiplexer #(.width(32), .enable("false")) multiplexer_6 (
    .in0({alu_1_out_4[31:14], alu_1_out_4_2, alu_1_out_4[1:0]}), .in1(ram_1_data), .out(out_1),
    .sel(control_unit_1_mem2reg));

  // Notes on the sheet:
  //   contents of rom_1 (hex, n*v repeats v):
  //   a00293 900313 628863 138393 b20213 8000e7
  //   RS1
  //   PC
  //   PC+4
  //   0
endmodule
